# Fritzing sketch MODULOb (saved by Fritzing 0.9.3b)
breadboards: 1

parts:
  Componente1 = Arduino Uno (Rev3)
  R1 = Resistor [tolerance=±5% resistance=220 package=THT]
  R2 = Resistor [tolerance=±5% resistance=220 package=THT]
  LED1 = LED - 5mm [color="Red (633nm)" package="5 mm [THT]"]
  LED2 = LED - 5mm [color="Red (633nm)" package="5 mm [THT]"]
  Componente2 = Bluetooth HC-05 Macho
  R3 = Resistor [tolerance=±5% resistance=2.2k package=THT]
  R4 = Resistor [tolerance=±5% resistance=1 package=THT]

nets:
  N1: Componente1.D12/MISO, LED1.anode
  N2: Componente1.D13/SCK, LED2.anode
  GND: Componente1.GND, R1.Pin_0, R2.Pin_0, Componente2.GND, R3.Pin_0
  N3: Componente1.D0/RX, Componente2.TXD
  N4: Componente1.D1/TX, R4.Pin_1
  5V: Componente1.5V, Componente2.VCC
  N5: R1.Pin_1, LED2.cathode
  N6: R2.Pin_1, LED1.cathode
  N7: Componente2.RXD, R3.Pin_1, R4.Pin_0
