# Fritzing sketch superMaquina (saved by Fritzing 0.9.3b)
circuit board: 8.46667cm x 5.64444cm
breadboards: 1

parts:
  LED1 = LED - 5mm [color="Red (633nm)" package="5 mm [THT]"]
  R1 = Resistor [tolerance=±5% resistance=330 package=THT]
  Componente1 = Arduino Uno (Rev3)

nets:
  N1: LED1.cathode, R1.Pin_1
  N2: LED1.anode, Componente1.D13/SCK
  N3: R1.Pin_0, Componente1.GND

// code stored in the sketch: sketch_aug20a.ino
/**
   SEQUENCIAL DE LEDS (EFEITO SUPER MAQUINA)
   @AUTOR - RAFAEL OLIVEIRA DE SOUZA
*/

void setup() {

  pinMode(13, OUTPUT);

}

void loop() {

  digitalWrite (13, HIGH);

  
}
